// Logisim project vichitator_rez.circ as structural Verilog: 1 circuit, main circuit main
module main (
  input  in_1,
  output [2:0] out_2
);

  wire and_1_out, h1_qn, h2_qn;

  and and_1 (and_1_out, h1_qn, h2_qn);
  T_Flip_Flop h3 (.T(and_1_out), .clk(in_1), .Q(out_2[2]));  // open: Qn, reset, preset
  T_Flip_Flop h2 (.T(h1_qn), .clk(in_1), .Q(out_2[1]), .Qn(h2_qn));  // open: reset, preset
  T_Flip_Flop h1 (.T(in_1), .clk(in_1), .Q(out_2[0]), .Qn(h1_qn));  // open: reset, preset
endmodule
